// Logisim project hw3.circ as structural Verilog: 12 circuits, main circuit part1
module my_circuit (
  input  in_1,
  input  in_2,
  input  in_3,
  output out_4,
  output out_5
);

  wire and_1_out, and_2_out, and_3_out, and_4_out, and_5_out, and_6_out, and_7_out, not_1_out, not_2_out,
       not_3_out;

  not not_1 (not_1_out, in_1);
  not not_2 (not_2_out, in_2);
  not not_3 (not_3_out, in_3);
  and and_1 (and_1_out, not_1_out, not_2_out, in_3);
  and and_2 (and_2_out, not_1_out, in_2, not_3_out);
  and and_3 (and_3_out, in_1, not_2_out, not_3_out);
  and and_4 (and_4_out, in_1, in_2, in_3);
  and and_5 (and_5_out, in_1, in_2);
  and and_6 (and_6_out, in_1, in_3);
  and and_7 (and_7_out, in_2, in_3);
  or or_1 (out_4, and_1_out, and_2_out, and_3_out, and_4_out);
  or or_2 (out_5, and_5_out, and_6_out, and_7_out);

  // Other names for the same wires on the sheet: A = in_1; B = in_2; C_in = in_3; C_out = out_5; S = out_4
endmodule

module part1 (
  input  in_1,
  input  in_2,
  input  in_3,
  output out_4,
  output out_5
);

  wire and_1_out, and_2_out, and_3_out, and_4_out, and_5_out, and_6_out, and_7_out, not_1_out, not_2_out,
       not_3_out;

  not not_1 (not_1_out, in_1);
  not not_2 (not_2_out, in_2);
  not not_3 (not_3_out, in_3);
  and and_1 (and_1_out, in_1, not_2_out, not_3_out);
  and and_2 (and_2_out, not_1_out, in_2, not_3_out);
  and and_3 (and_3_out, not_1_out, not_2_out, in_3);
  and and_4 (and_4_out, in_1, in_2, in_3);
  and and_5 (and_5_out, in_1, in_2);
  and and_6 (and_6_out, in_1, in_3);
  and and_7 (and_7_out, in_2, in_3);
  or or_1 (out_4, and_1_out, and_2_out, and_3_out, and_4_out);
  or or_2 (out_5, and_5_out, and_6_out, and_7_out);

  // Other names for the same wires on the sheet: A = in_1; B = in_2; Carry_in = in_3; Carry_out = out_5; Sum = out_4

  // Notes on the sheet:
  //   Jeongoo Kim
  //   903093035
endmodule

module part2 (
  input  [3:0] in_1,
  input  [3:0] in_2,
  input  in_3,
  output [3:0] out_4,
  output out_5
);

  wire part1_1_out_5, part1_2_out_5, part1_3_out_5;

  part1 part1_1 (.out_4(out_4[0]), .in_1(in_1[0]), .out_5(part1_1_out_5), .in_2(in_2[0]), .in_3(in_3));
  part1 part1_2 (.out_4(out_4[1]), .in_1(in_1[1]), .out_5(part1_2_out_5), .in_2(in_2[1]), .in_3(part1_1_out_5));
  part1 part1_3 (.out_4(out_4[2]), .in_1(in_1[2]), .out_5(part1_3_out_5), .in_2(in_2[2]), .in_3(part1_2_out_5));
  part1 part1_4 (.out_4(out_4[3]), .in_1(in_1[3]), .out_5(out_5), .in_2(in_2[3]), .in_3(part1_3_out_5));

  // Other names for the same wires on the sheet: A[3:0] = in_1; B[3:0] = in_2; Carry_in = in_3; Carry_out = out_5;
  //   Sum[3:0] = out_4

  // Notes on the sheet:
  //   Jeongoo Kim
  //   903093035
endmodule

module part3 (
  input  [3:0] A,
  input  [3:0] B,
  input  In,
  input  in_4,
  input  in_5,
  input  in_6,
  output Out,
  output [3:0] out_8
);

  wire [3:0] Addiction_out_4, AND_out, Decreament_out_3, Multiply_by_4_out_2, Negation_out_2, OR_out,
       Subtract_out_3, XOR_out;

  part2 Addiction (.in_1(A), .in_2(B), .in_3(In), .out_4(Addiction_out_4), .out_5(Out));
  _4bits_Negation Negation (.out_2(Negation_out_2), .\input (A));
  _4bits_Multiply_by_4 Multiply_by_4 (.out_2(Multiply_by_4_out_2), .in_1(A));
  _4bits_subtract Subtract (.in_1(A), .in_2(B), .out_3(Subtract_out_3));
  _4bits_subtract Decreament (.in_1(A), .in_2(4'b0001), .out_3(Decreament_out_3));
  assign AND_out = A & B;  // AND_Gate AND, 4 bits wide
  assign OR_out = A | B;  // OR_Gate OR, 4 bits wide
  assign XOR_out = A ^ B;  // XOR_Gate XOR, 4 bits wide
  Multiplexer #(.select(3), .width(4), .disabled(0), .enable("false")) multiplexer_1 (
    .in0(Addiction_out_4), .in1(Subtract_out_3), .in2(Decreament_out_3), .in3(Negation_out_2),
    .in4(Multiply_by_4_out_2), .in5(AND_out), .in6(OR_out), .in7(XOR_out), .out(out_8),
    .sel({in_4, in_5, in_6}));

  // Notes on the sheet:
  //   Jeongoo Kim
  //   903093035
endmodule

module _4bits_subtract (
  input  [3:0] in_1,
  input  [3:0] in_2,
  output [3:0] out_3
);

  wire [3:0] n4bits_negation_1_out_2;

  _4bits_Negation u_4bits_negation_1 (.out_2(n4bits_negation_1_out_2), .\input (in_2));
  part2 part2_1 (.in_1(in_1), .in_2(n4bits_negation_1_out_2), .in_3(1'b0), .out_4(out_3));  // open: out_5
endmodule

module _4bits_Negation (
  input  [3:0] \input ,
  output [3:0] out_2
);

  wire [3:0] not_1_out;

  assign not_1_out = ~\input ;  // NOT_Gate not_1, 4 bits wide
  part2 part2_1 (.in_1(4'b0001), .in_2(not_1_out), .in_3(1'b0), .out_4(out_2));  // open: out_5
endmodule

module _4bits_Multiply_by_4 (
  input  [3:0] in_1,
  output [3:0] out_2
);


  assign out_2 = {in_1[1:0], 2'b00};
endmodule

module part4 (
  input  In,
  input  [15:0] A,
  input  [15:0] B,
  input  in_4,
  input  in_5,
  input  in_6,
  output out_7,
  output [15:0] out_8
);

  wire [15:0] Addiction_out_5, AND_out, Decreament_out_3, Multiply_by_4_out_2, Negation_out_2, OR_out,
       Subtract_out_3, XOR_out;

  _16bits_Subtract Subtract (.in_2(A), .in_1(B), .out_3(Subtract_out_3));
  _16bits_Negation Negation (.in_1(A), .out_2(Negation_out_2));
  _16bits_Multiply_by_4 Multiply_by_4 (.out_2(Multiply_by_4_out_2), .in_1(A));
  _16bits_Adder Addiction (.out_4(out_7), .in_2(A), .in_3(B), .in_1(In), .out_5(Addiction_out_5));
  _16bits_Subtract Decreament (.in_2(A), .in_1(16'h1), .out_3(Decreament_out_3));
  assign AND_out = A & B;  // AND_Gate AND, 16 bits wide
  assign OR_out = A | B;  // OR_Gate OR, 16 bits wide
  assign XOR_out = A ^ B;  // XOR_Gate XOR, 16 bits wide
  Multiplexer #(.select(3), .width(16), .disabled(0), .enable("false")) multiplexer_1 (
    .in0(Addiction_out_5), .in1(Subtract_out_3), .in2(Decreament_out_3), .in3(Negation_out_2),
    .in4(Multiply_by_4_out_2), .in5(AND_out), .in6(OR_out), .in7(XOR_out), .out(out_8),
    .sel({in_4, in_5, in_6}));

  // Notes on the sheet:
  //   Jeongoo Kim
  //   903093035
endmodule

module _16bits_Adder (
  input  in_1,
  input  [15:0] in_2,
  input  [15:0] in_3,
  output out_4,
  output [15:0] out_5
);

  wire part2_1_out_5, part2_2_out_5, part2_3_out_5;

  part2 part2_1 (.in_1(in_2[3:0]), .in_2(in_3[3:0]), .in_3(in_1), .out_4(out_5[3:0]), .out_5(part2_1_out_5));
  part2 part2_2 (.in_1(in_2[7:4]), .in_2(in_3[7:4]), .in_3(part2_1_out_5), .out_4(out_5[7:4]), .out_5(part2_2_out_5));
  part2 part2_3 (
    .in_1(in_2[11:8]), .in_2(in_3[11:8]), .in_3(part2_2_out_5), .out_4(out_5[11:8]), .out_5(part2_3_out_5));
  part2 part2_4 (.in_1(in_2[15:12]), .in_2(in_3[15:12]), .in_3(part2_3_out_5), .out_4(out_5[15:12]), .out_5(out_4));
endmodule

module _16bits_Negation (
  input  [15:0] in_1,
  output [15:0] out_2
);

  wire [15:0] not_1_out;

  assign not_1_out = ~in_1;  // NOT_Gate not_1, 16 bits wide
  _16bits_Adder u_16bits_adder_1 (.in_2(16'h1), .in_3(not_1_out), .in_1(1'b0), .out_5(out_2));  // open: out_4
endmodule

module _16bits_Subtract (
  input  [15:0] in_1,
  input  [15:0] in_2,
  output [15:0] out_3
);

  wire [15:0] n16bits_negation_1_out_2;

  _16bits_Negation u_16bits_negation_1 (.in_1(in_1), .out_2(n16bits_negation_1_out_2));
  _16bits_Adder u_16bits_adder_1 (
    .in_2(in_2), .in_3(n16bits_negation_1_out_2), .in_1(1'b0), .out_5(out_3));  // open: out_4
endmodule

module _16bits_Multiply_by_4 (
  input  [15:0] in_1,
  output [15:0] out_2
);


  assign out_2 = {in_1[13:0], 2'b00};
endmodule
