// Logisim project hw4part2.circ as structural Verilog: 2 circuits, main circuit One-Hot State Machine
module Tester (
  input  G
);

  wire Clock_out, one_hot_state_machine_1_w, one_hot_state_machine_1_x, one_hot_state_machine_1_y,
       one_hot_state_machine_1_z, Reset_out;

  One_Hot_State_Machine one_hot_state_machine_1 (
    .W(one_hot_state_machine_1_w), .Clock(Clock_out), .Reset(Reset_out), .G(G),
    .X(one_hot_state_machine_1_x), .Y(one_hot_state_machine_1_y), .Z(one_hot_state_machine_1_z));  // open: out_8
  Clock Clock (.out(Clock_out));
  Button Reset (.out(Reset_out));
  LED W (.in(one_hot_state_machine_1_w));
  LED X (.in(one_hot_state_machine_1_x));
  LED Y (.in(one_hot_state_machine_1_y));
  LED Z (.in(one_hot_state_machine_1_z));

  // Notes on the sheet:
  //   You can use this to test your circuit.
endmodule

module One_Hot_State_Machine (
  input  G,
  input  Clock,
  input  Reset,
  output W,
  output X,
  output Y,
  output Z,
  output [6:0] out_8
);

  wire and_1_out, and_2_out, and_3_out, and_5_out, and_8_out, nor_1_out;
  wire [6:0] or_4_out;

  or or_1 (or_4_out[6], and_2_out, out_8[5]);
  or or_2 (or_4_out[5], out_8[4], and_3_out);
  or or_3 (or_4_out[3], and_5_out, out_8[2]);
  or or_4 (or_4_out[0], and_8_out, and_1_out, nor_1_out);
  and and_1 (and_1_out, ~G, out_8[6]);  // AND_Gate
  and and_2 (and_2_out, G, out_8[6]);
  and and_3 (and_3_out, G, out_8[3]);
  and and_4 (or_4_out[4], G, out_8[1]);
  and and_5 (and_5_out, ~G, out_8[3]);  // AND_Gate
  and and_6 (or_4_out[2], ~G, out_8[1]);  // AND_Gate
  and and_7 (or_4_out[1], G, out_8[0]);
  and and_8 (and_8_out, ~G, out_8[0]);  // AND_Gate
  Register #(.width(7)) register_1 (.D(or_4_out), .Q(out_8), .clk(Clock), .clr(Reset));  // open: en
  nor nor_1 (nor_1_out, out_8[0], out_8[1], out_8[2], out_8[3], out_8[4], out_8[5], out_8[6]);
  or or_5 (W, out_8[2], out_8[3], out_8[6]);
  or or_6 (X, out_8[0], out_8[3]);
  or or_7 (Y, out_8[3], out_8[5], out_8[6]);
  or or_8 (Z, out_8[2], out_8[4], out_8[5]);

  // Other names for the same wires on the sheet: CLK = Clock; RST = Reset

  // Notes on the sheet:
  //   My name is
  //   Jeongsoo Kim
  //   Implement your one-hot state machine circuit here!
  //   and this is my pretty one-hot state machine!
endmodule
