// Logisim project Kim_Jeongsoo.circ as structural Verilog: 13 circuits, main circuit main
module main (
  output [1:0] out_1,
  output [31:0] out_2,
  output [31:0] out_3,
  output [31:0] out_4,
  output [31:0] A,
  output [31:0] B,
  output [31:0] EX_RES_DB,
  output [3:0] out_8,
  output [3:0] out_9,
  output [3:0] out_10,
  output [3:0] out_11,
  output [31:0] out_12,
  output [19:0] out_13,
  output [3:0] out_14,
  output [31:0] out_15,
  output [19:0] OFFSET,
  output [3:0] out_17,
  output [3:0] OP,
  output [3:0] OP_2,
  output [3:0] out_20,
  output [31:0] out_21,
  output [3:0] out_22,
  output [31:0] out_23,
  output [31:0] out_24,
  output [31:0] out_25,
  output [31:0] out_26,
  output [31:0] out_27,
  output [1:0] out_28,
  output [3:0] out_29,
  output [3:0] out_30,
  output [3:0] out_31,
  output [3:0] out_32,
  output [31:0] out_33,
  output [3:0] out_34,
  output [3:0] out_35,
  output [31:0] out_36,
  output [31:0] out_37,
  output [31:0] out_38
);

  wire and_3_out, and_4_out, beq_EX, beq_ID, BEQ_ON, clear, clock, flush, Halt, jalr_ID, LD_MEM, lw_EX,
       LW_WB, NOOP, not_1_out, not_2_out, Off, or_1_out, stall, sw_ID, SW_MEM, WrEn;
  wire [1:1] or_2_out;
  wire [3:0] controlled_buffer_5_out, OP_WB;
  wire [19:0] idrr_ex_buffer_1_offset_out;
  wire [31:0] adder_1_out, alu_2_out, controlled_buffer_1_out, controlled_buffer_2_out,
       controlled_buffer_3_out, dual_ported_register_file_1_out1, dual_ported_register_file_1_out2,
       idrr_ex_buffer_1_pc_output, if_idrr_buffer_1_inst_output, if_idrr_buffer_1_pc_output, MEM_FOR, PC_q,
       ram_2_data, SW_VAL;

  not not_1 (not_1_out, stall);
  Clock clock_1 (.out(clock));
  Button button_1 (.out(clear));
  Register #(.width(32)) PC (.D(out_2), .en(not_1_out), .Q(PC_q), .clk(clock), .clr(clear));
  Multiplexer #(.select(2), .width(32), .enable("false")) multiplexer_1 (
    .in0(adder_1_out), .in1(out_21), .in2(controlled_buffer_1_out), .out(out_2), .sel(out_1));  // open: in3
  Adder #(.width(32)) adder_1 (.a(PC_q), .b(32'h1), .out(adder_1_out));  // open: cin, cout
  RAM #(.addrWidth(24), .dataWidth(32)) ram_1 (.addr(PC_q[23:0]), .data(out_12));  // open: sel, clk, ld, clr
  Comparator #(.width(32)) comparator_1 (.b(32'h70000000), .eq(Halt));  // open: a, gt, lt
  IF_IDRR_Buffer if_idrr_buffer_1 (
    .clear(clear), .stall(stall), .PC_INPUT(adder_1_out), .INST_INPUT(out_12),
    .PC_OUTPUT(if_idrr_buffer_1_pc_output), .clock(clock), .INST_OUTPUT(if_idrr_buffer_1_inst_output),
    .flush(flush));
  Bit_SP bit_sp_1 (
    .INST_INPUT(if_idrr_buffer_1_inst_output), .RZ(out_20), .OFFSET(OFFSET), .RY(out_11), .RX(out_9),
    .OPCODE(OP));
  Multiplexer #(.width(4), .enable("false")) multiplexer_2 (.in0(out_20), .in1(out_9), .out(out_17), .sel(or_1_out));
  and and_1 (out_1[0], BEQ_ON, beq_EX);
  or or_1 (or_1_out, jalr_ID, beq_ID, sw_ID);
  Control_SIG control_sig_1 (
    .Opcode(OP), .JALR(jalr_ID), .BEQ(beq_ID), .SW(sw_ID));  // open: WrEn, LW, FUNC, NAND, OFF, HALT
  // AND_Gate and_2 is placed but not wired
  Dual_Ported_Register_File dual_ported_register_file_1 (
    .CLK(clock), .WrREGNO(out_22), .RdREGNO1(out_11), .RdREGNO2(out_17), .INPUT(out_27),
    .OUT1(dual_ported_register_file_1_out1), .OUT2(dual_ported_register_file_1_out2), .WrEN(WrEn));
  Forwarding forwarding_1 (
    .Ry(out_11), .Rz(out_17), .RxE(out_31), .RxM(out_30), .RxW(out_22),
    .A_in(dual_ported_register_file_1_out1), .B_in(dual_ported_register_file_1_out2), .E_in(out_38),
    .M_in(MEM_FOR), .W_in(out_27), .A_OUT(A), .B_OUT(B));  // open: out_11, out_13
  Multiplexer #(.select(2), .width(4), .enable("false")) multiplexer_3 (
    .in0(out_9), .in1(out_11), .in2(4'b0000), .in3(4'b0000), .out(OP_2), .sel({or_2_out[1], jalr_ID}));
  or or_2 (or_2_out[1], sw_ID, beq_ID);
  LW_STALL lw_stall_1 (
    .LW_EX(lw_EX), .LW_DEST(out_31), .A_REG(out_11), .B_REG(out_17), .ID_OP(OP), .sw_ID(sw_ID),
    .stall(stall), .NOOP(NOOP));
  IDRR_EX_Buffer idrr_ex_buffer_1 (
    .clock(clock), .clear(clear), .PC_Input(if_idrr_buffer_1_pc_output), .A_Input(A), .B_Input(B),
    .Offset_In(OFFSET), .Opcode_In(OP), .Rx_Dest_In(OP_2), .PC_Output(idrr_ex_buffer_1_pc_output),
    .A_Output(out_4), .B_Output(out_33), .Offset_Out(idrr_ex_buffer_1_offset_out), .Opcode_Out(out_10),
    .Rx_Dest_Out(out_31), .flush(flush), .NOOP(NOOP));
  assign out_3 = {{12{idrr_ex_buffer_1_offset_out[19]}}, idrr_ex_buffer_1_offset_out};  // Bit_Extender bit_extender_1
  assign controlled_buffer_1_out = out_1[1] ? out_33 : 32'bz;  // Controlled_Buffer controlled_buffer_1
  assign controlled_buffer_2_out = beq_EX ? idrr_ex_buffer_1_pc_output : 32'bz;  // Controlled_Buffer controlled_buffer_2
  assign controlled_buffer_3_out = beq_EX ? out_3 : 32'bz;  // Controlled_Buffer controlled_buffer_3
  Control_SIG control_sig_2 (
    .Opcode(out_10), .JALR(out_1[1]), .BEQ(beq_EX), .LW(lw_EX), .FUNC(out_28), .OFF(Off), .HALT(Halt));  // open: WrEn, SW, NAND
  and and_3 (and_3_out, BEQ_ON, beq_EX);
  Multiplexer #(.width(32), .enable("false")) multiplexer_4 (.in0(out_33), .in1(out_3), .out(out_37), .sel(Off));
  or or_3 (flush, out_1[1], and_3_out);
  ALU alu_1 (.FUNC(out_28), .A(out_4), .B(out_37), .OUT(EX_RES_DB));
  Comparator #(.width(32)) comparator_2 (.a(EX_RES_DB), .b({32{1'b0}}), .eq(BEQ_ON));  // open: gt, lt
  and and_4 (and_4_out, beq_EX, BEQ_ON);
  ALU alu_2 (.FUNC(2'b00), .A(controlled_buffer_2_out), .B(controlled_buffer_3_out), .OUT(alu_2_out));
  assign out_21 = and_4_out ? alu_2_out : 32'bz;  // Controlled_Buffer BEQ_PC
  Multiplexer #(.width(32), .enable("false")) multiplexer_5 (
    .in0(EX_RES_DB), .in1(idrr_ex_buffer_1_pc_output), .out(out_38), .sel(out_1[1]));
  EX_MEM_Buffer ex_mem_buffer_1 (
    .clock(clock), .clear(clear), .EX_INPUT(out_38), .B_INPUT(out_33), .Rx_DEST_IN(out_31), .OP_IN(out_10),
    .EX_OUTPUT(out_25), .B_OUTPUT(SW_VAL), .Rx_DEST_OUT(out_30), .OP_OUT(out_29));
  assign out_15 = SW_MEM ? SW_VAL : 32'bz;  // Controlled_Buffer SW_BUF
  Control_SIG control_sig_3 (
    .Opcode(out_29), .SW(SW_MEM), .LW(LD_MEM));  // open: WrEn, JALR, BEQ, FUNC, NAND, OFF, HALT
  Multiplexer #(.width(32), .enable("false")) multiplexer_6 (.in0(out_25), .in1(out_26), .out(MEM_FOR), .sel(LD_MEM));
  RAM #(.addrWidth(24), .dataWidth(32), .bus("separate")) ram_2 (
    .addr(out_25[23:0]), .din(out_15), .data(ram_2_data), .str(SW_MEM), .clk(clock), .ld(LD_MEM));  // open: sel, clr
  assign out_26 = LD_MEM ? ram_2_data : 32'bz;  // Controlled_Buffer controlled_buffer_4
  MEM_WB_Buffer mem_wb_buffer_1 (
    .clock(clock), .clear(clear), .EX_INPUT(out_25), .DRAM_INPUT(out_26), .OPCODE(out_29),
    .DEST_INPUT(controlled_buffer_5_out), .EX_OUTPUT(out_23), .DRAM_OUTPUT(out_24), .OPCODE_2(OP_WB),
    .DEST_OUPUT(out_22));
  assign controlled_buffer_5_out = not_2_out ? out_30 : 4'bz;  // Controlled_Buffer controlled_buffer_5
  not not_2 (not_2_out, SW_MEM);
  Control_SIG control_sig_4 (.Opcode(OP_WB), .WrEn(WrEn), .LW(LW_WB));  // open: JALR, BEQ, SW, FUNC, NAND, OFF, HALT
  Multiplexer #(.width(32), .enable("false")) multiplexer_7 (.in0(out_23), .in1(out_24), .out(out_27), .sel(LW_WB));
  Comparator #(.width(4)) comparator_3 (.a(OP_WB), .b(4'b0011));  // open: gt, eq, lt

  assign out_8 = OP;
  assign out_13 = OFFSET;
  assign out_14 = out_11;
  assign out_32 = out_10;
  assign out_34 = out_22;
  assign out_35 = out_11;
  assign out_36 = out_3;

  // Other names for the same wires on the sheet: B_EX[31:0] = out_33; B_Reg[3:0] = out_17; DEST_EX[3:0] = out_31;
  //   DEST_MEM[3:0] = out_30; DEST_WB[3:0] = out_22; DVAL_WB[31:0] = out_24; EVal[31:0] = out_38;
  //   EVAL_WB[31:0] = out_23; EX_Val[31:0] = out_25; func[1:0] = out_28; LdMEM = LD_MEM; MEM_Val[31:0] = out_26;
  //   OFF_DB[31:0] = out_3; OFF_DB_2[31:0] = out_37; Op_EX[3:0] = out_10; OP_MEM[3:0] = out_29; Opcode[3:0] = OP;
  //   PC_From[1:0] = out_1; jalr_EX = out_1[1]; Rx[3:0] = out_9; A_Reg[3:0] = out_11; Ry[3:0] = out_11;
  //   Rz[3:0] = out_20; WB_VAL[31:0] = out_27; SW_MEM_DEST = SW_MEM; WrMEM = SW_MEM

  // Notes on the sheet:
  //   PC ADDER
  //   INST MEMORY
  //   0 Normal PC
  //   1 BEQ PC
  //   2 JALR PC
  //   PC_MUX_SEL
  //   LW_Stall & Flush
  //   JALR & BEQ FLUSH
endmodule

module Dual_Ported_Register_File (
  input  CLK,
  input  WrEN,
  input  [3:0] WrREGNO,
  input  [3:0] RdREGNO1,
  input  [3:0] RdREGNO2,
  input  [31:0] INPUT,
  output [31:0] OUT1,
  output [31:0] OUT2
);

  wire En_a0, En_a1, En_a2, En_a3, En_a4, En_at, En_fp, En_k0, En_ra, En_s0, En_s1, En_s2, En_s3, En_sp,
       En_v0;
  wire [31:0] a0, a1, a2, a3, a4, at, fp, k0, ra, s0, s1, s2, s3, sp, v0, zero;

  Decoder #(.select(4), .disabled(0)) decoder_1 (
    .out1(En_at), .out2(En_v0), .out3(En_a0), .out4(En_a1), .out5(En_a2), .out6(En_a3), .out7(En_a4),
    .out8(En_s0), .out9(En_s1), .out10(En_s2), .out11(En_s3), .out12(En_k0), .out13(En_sp), .out14(En_fp),
    .out15(En_ra), .sel(WrREGNO), .en(WrEN));  // open: out0
  Register #(.width(32)) u_zero (.D(INPUT), .en(1'b0), .Q(zero), .clk(CLK));  // open: clr
  Register #(.width(32)) u_at (.D(INPUT), .en(En_at), .Q(at), .clk(CLK));  // open: clr
  Register #(.width(32)) u_v0 (.D(INPUT), .en(En_v0), .Q(v0), .clk(CLK));  // open: clr
  Register #(.width(32)) u_a0 (.D(INPUT), .en(En_a0), .Q(a0), .clk(CLK));  // open: clr
  Register #(.width(32)) u_a1 (.D(INPUT), .en(En_a1), .Q(a1), .clk(CLK));  // open: clr
  Register #(.width(32)) u_a2 (.D(INPUT), .en(En_a2), .Q(a2), .clk(CLK));  // open: clr
  Register #(.width(32)) u_a3 (.D(INPUT), .en(En_a3), .Q(a3), .clk(CLK));  // open: clr
  Register #(.width(32)) u_a4 (.D(INPUT), .en(En_a4), .Q(a4), .clk(CLK));  // open: clr
  Multiplexer #(.select(4), .width(32), .disabled(0), .enable("false")) multiplexer_1 (
    .in0(zero), .in1(at), .in2(v0), .in3(a0), .in4(a1), .in5(a2), .in6(a3), .in7(a4), .in8(s0), .in9(s1),
    .in10(s2), .in11(s3), .in12(k0), .in13(sp), .in14(fp), .in15(ra), .out(OUT2), .sel(RdREGNO2));
  Register #(.width(32)) u_s0 (.D(INPUT), .en(En_s0), .Q(s0), .clk(CLK));  // open: clr
  Register #(.width(32)) u_s1 (.D(INPUT), .en(En_s1), .Q(s1), .clk(CLK));  // open: clr
  Register #(.width(32)) u_s2 (.D(INPUT), .en(En_s2), .Q(s2), .clk(CLK));  // open: clr
  Register #(.width(32)) u_s3 (.D(INPUT), .en(En_s3), .Q(s3), .clk(CLK));  // open: clr
  Register #(.width(32)) u_k0 (.D(INPUT), .en(En_k0), .Q(k0), .clk(CLK));  // open: clr
  Register #(.width(32)) u_sp (.D(INPUT), .en(En_sp), .Q(sp), .clk(CLK));  // open: clr
  Register #(.width(32)) u_fp (.D(INPUT), .en(En_fp), .Q(fp), .clk(CLK));  // open: clr
  Register #(.width(32)) u_ra (.D(INPUT), .en(En_ra), .Q(ra), .clk(CLK));  // open: clr
  Multiplexer #(.select(4), .width(32), .disabled(0), .enable("false")) multiplexer_2 (
    .in0(zero), .in1(at), .in2(v0), .in3(a0), .in4(a1), .in5(a2), .in6(a3), .in7(a4), .in8(s0), .in9(s1),
    .in10(s2), .in11(s3), .in12(k0), .in13(sp), .in14(fp), .in15(ra), .out(OUT1), .sel(RdREGNO1));

  // Notes on the sheet:
  //   MODIFY AT YOUR OWN RISK
endmodule

module IF_IDRR_Buffer (
  input  clock,
  input  clear,
  input  stall,
  input  flush,
  input  [31:0] PC_INPUT,
  input  [31:0] INST_INPUT,
  output [31:0] PC_OUTPUT,
  output [31:0] INST_OUTPUT
);

  wire not_1_out, not_2_out;
  wire [31:0] multiplexer_1_out, multiplexer_2_out;

  Multiplexer #(.width(32), .enable("false")) multiplexer_1 (
    .in0(PC_INPUT), .in1({32{1'b0}}), .out(multiplexer_1_out), .sel(flush));
  not not_1 (not_1_out, stall);
  Register #(.width(32)) register_1 (.D(multiplexer_1_out), .en(not_1_out), .Q(PC_OUTPUT), .clk(clock), .clr(clear));
  not not_2 (not_2_out, stall);
  Multiplexer #(.width(32), .enable("false")) multiplexer_2 (
    .in0(INST_INPUT), .in1({32{1'b0}}), .out(multiplexer_2_out), .sel(flush));
  Register #(.width(32)) register_2 (.D(multiplexer_2_out), .en(not_2_out), .Q(INST_OUTPUT), .clk(clock), .clr(clear));
endmodule

module IDRR_EX_Buffer (
  input  clock,
  input  clear,
  input  flush,
  input  NOOP,
  input  [31:0] PC_Input,
  input  [31:0] A_Input,
  input  [31:0] B_Input,
  input  [19:0] Offset_In,
  input  [3:0] Opcode_In,
  input  [3:0] Rx_Dest_In,
  output [31:0] PC_Output,
  output [31:0] A_Output,
  output [31:0] B_Output,
  output [19:0] Offset_Out,
  output [3:0] Opcode_Out,
  output [3:0] Rx_Dest_Out
);

  wire or_1_out, or_2_out, or_3_out, or_4_out, or_5_out, or_6_out;
  wire [3:0] multiplexer_5_out, multiplexer_6_out;
  wire [19:0] multiplexer_4_out;
  wire [31:0] multiplexer_1_out, multiplexer_2_out, multiplexer_3_out;

  or or_1 (or_1_out, NOOP, flush);
  or or_2 (or_2_out, NOOP, flush);
  or or_3 (or_3_out, NOOP, flush);
  or or_4 (or_4_out, NOOP, flush);
  or or_5 (or_5_out, NOOP, flush);
  or or_6 (or_6_out, NOOP, flush);
  Multiplexer #(.width(32), .enable("false")) multiplexer_1 (
    .in0(PC_Input), .in1({32{1'b0}}), .out(multiplexer_1_out), .sel(or_1_out));
  Multiplexer #(.width(32), .enable("false")) multiplexer_2 (
    .in0(A_Input), .in1({32{1'b0}}), .out(multiplexer_2_out), .sel(or_2_out));
  Multiplexer #(.width(32), .enable("false")) multiplexer_3 (
    .in0(B_Input), .in1({32{1'b0}}), .out(multiplexer_3_out), .sel(or_3_out));
  Multiplexer #(.width(20), .enable("false")) multiplexer_4 (
    .in0(Offset_In), .in1({20{1'b0}}), .out(multiplexer_4_out), .sel(or_4_out));
  Multiplexer #(.width(4), .enable("false")) multiplexer_5 (
    .in0(Opcode_In), .in1(4'b0000), .out(multiplexer_5_out), .sel(or_5_out));
  Multiplexer #(.width(4), .enable("false")) multiplexer_6 (
    .in0(Rx_Dest_In), .in1(4'b0000), .out(multiplexer_6_out), .sel(or_6_out));
  Register #(.width(32)) register_1 (.D(multiplexer_1_out), .en(clock), .Q(PC_Output), .clk(clock), .clr(clear));
  Register #(.width(32)) register_2 (.D(multiplexer_2_out), .en(clock), .Q(A_Output), .clk(clock), .clr(clear));
  Register #(.width(32)) register_3 (.D(multiplexer_3_out), .en(clock), .Q(B_Output), .clk(clock), .clr(clear));
  Register #(.width(20)) register_4 (.D(multiplexer_4_out), .en(clock), .Q(Offset_Out), .clk(clock), .clr(clear));
  Register #(.width(4)) register_5 (.D(multiplexer_5_out), .en(clock), .Q(Opcode_Out), .clk(clock), .clr(clear));
  Register #(.width(4)) register_6 (.D(multiplexer_6_out), .en(clock), .Q(Rx_Dest_Out), .clk(clock), .clr(clear));
endmodule

module EX_MEM_Buffer (
  input  clock,
  input  clear,
  input  [31:0] EX_INPUT,
  input  [31:0] B_INPUT,
  input  [3:0] Rx_DEST_IN,
  input  [3:0] OP_IN,
  output [31:0] EX_OUTPUT,
  output [31:0] B_OUTPUT,
  output [3:0] Rx_DEST_OUT,
  output [3:0] OP_OUT
);

  wire not_1_out, not_2_out, not_3_out, not_4_out;

  not not_1 (not_1_out, clear);
  not not_2 (not_2_out, clear);
  not not_3 (not_3_out, clear);
  not not_4 (not_4_out, clear);
  Register #(.width(32)) register_1 (.D(EX_INPUT), .en(not_1_out), .Q(EX_OUTPUT), .clk(clock), .clr(clear));
  Register #(.width(32)) register_2 (.D(B_INPUT), .en(not_2_out), .Q(B_OUTPUT), .clk(clock), .clr(clear));
  Register #(.width(4)) register_3 (.D(Rx_DEST_IN), .en(not_3_out), .Q(Rx_DEST_OUT), .clk(clock), .clr(clear));
  Register #(.width(4)) register_4 (.D(OP_IN), .en(not_4_out), .Q(OP_OUT), .clk(clock), .clr(clear));
endmodule

module MEM_WB_Buffer (
  input  clock,
  input  clear,
  input  [31:0] EX_INPUT,
  input  [31:0] DRAM_INPUT,
  input  [3:0] OPCODE,
  input  [3:0] DEST_INPUT,
  output [31:0] EX_OUTPUT,
  output [31:0] DRAM_OUTPUT,
  output [3:0] OPCODE_2,
  output [3:0] DEST_OUPUT
);

  wire not_1_out, not_2_out, not_3_out, not_4_out;

  Register #(.width(32)) register_1 (.D(EX_INPUT), .en(not_1_out), .Q(EX_OUTPUT), .clk(clock), .clr(clear));
  not not_1 (not_1_out, clear);
  Register #(.width(32)) register_2 (.D(DRAM_INPUT), .en(not_2_out), .Q(DRAM_OUTPUT), .clk(clock), .clr(clear));
  not not_2 (not_2_out, clear);
  Register #(.width(4)) register_3 (.D(OPCODE), .en(not_3_out), .Q(OPCODE_2), .clk(clock), .clr(clear));
  not not_3 (not_3_out, clear);
  Register #(.width(4)) register_4 (.D(DEST_INPUT), .en(not_4_out), .Q(DEST_OUPUT), .clk(clock), .clr(clear));
  not not_4 (not_4_out, clear);
endmodule

module ALU (
  input  [1:0] FUNC,
  input  [31:0] A,
  input  [31:0] B,
  output [31:0] OUT
);

  wire [31:0] adder_1_out, adder_2_out, nand_1_out, subtractor_1_out;

  Adder #(.width(32)) adder_1 (.a(A), .b(B), .out(adder_1_out), .cin(1'b0));  // open: cout
  assign nand_1_out = ~(A & B);  // NAND_Gate nand_1, 32 bits wide
  Subtractor #(.width(32)) subtractor_1 (.a(A), .b(B), .out(subtractor_1_out), .bin(1'b0));  // open: bout
  Adder #(.width(32)) adder_2 (.a(A), .b({32{1'b0}}), .out(adder_2_out), .cin(1'b1));  // open: cout
  Multiplexer #(.select(2), .width(32), .disabled(0), .enable("false")) multiplexer_1 (
    .in0(adder_1_out), .in1(nand_1_out), .in2(subtractor_1_out), .in3(adder_2_out), .out(OUT), .sel(FUNC));

  // Notes on the sheet:
  //   MODIFY AT YOUR OWN RISK
endmodule

// BIT_SP
module Bit_SP (
  input  [31:0] INST_INPUT,
  output [3:0] RZ,
  output [19:0] OFFSET,
  output [3:0] RY,
  output [3:0] RX,
  output [3:0] OPCODE
);


  assign OFFSET = INST_INPUT[19:0];
  assign OPCODE = INST_INPUT[31:28];
  assign RX = INST_INPUT[27:24];
  assign RY = INST_INPUT[23:20];
  assign RZ = INST_INPUT[3:0];
endmodule

module Forwarding (
  input  [3:0] Ry,
  input  [3:0] Rz,
  input  [3:0] RxE,
  input  [3:0] RxM,
  input  [3:0] RxW,
  input  [31:0] A_in,
  input  [31:0] B_in,
  input  [31:0] E_in,
  input  [31:0] M_in,
  input  [31:0] W_in,
  output [2:0] out_11,
  output [31:0] A_OUT,
  output [2:0] out_13,
  output [31:0] B_OUT
);

  wire Ry_zero, RyE, RyM, RyW, Rz_zero, RzE, RzM, RzW;

  Comparator #(.width(4)) comparator_1 (.a(Ry), .b(RxE), .eq(RyE));  // open: gt, lt
  Comparator #(.width(4)) comparator_2 (.a(Ry), .b(RxM), .eq(RyM));  // open: gt, lt
  Comparator #(.width(4)) comparator_3 (.a(Ry), .b(RxW), .eq(RyW));  // open: gt, lt
  Multiplexer #(.width(3), .enable("false")) multiplexer_1 (
    .in0({RyE, RyM, RyW}), .in1(3'b000), .out(out_11), .sel(Ry_zero));
  Comparator #(.width(4)) comparator_4 (.a(Rz), .b(RxE), .eq(RzE));  // open: gt, lt
  Comparator #(.width(4)) comparator_5 (.a(Rz), .b(RxM), .eq(RzM));  // open: gt, lt
  Comparator #(.width(4)) comparator_6 (.a(Rz), .b(RxW), .eq(RzW));  // open: gt, lt
  Multiplexer #(.select(3), .width(32), .enable("false")) multiplexer_2 (
    .in0(A_in), .in1(W_in), .in2(M_in), .in3(M_in), .in4(E_in), .in5(E_in), .in6(E_in), .in7(E_in),
    .out(A_OUT), .sel(out_11));
  Multiplexer #(.width(3), .enable("false")) multiplexer_3 (
    .in0({RzE, RzM, RzW}), .in1(3'b000), .out(out_13), .sel(Rz_zero));
  Multiplexer #(.select(3), .width(32), .enable("false")) multiplexer_4 (
    .in0(B_in), .in1(W_in), .in2(M_in), .in3(M_in), .in4(E_in), .in5(E_in), .in6(E_in), .in7(E_in),
    .out(B_OUT), .sel(out_13));
  Comparator #(.width(4)) comparator_7 (.a(Ry), .b(4'b0000), .eq(Ry_zero));  // open: gt, lt
  Comparator #(.width(4)) comparator_8 (.a(Rz), .b(4'b0000), .eq(Rz_zero));  // open: gt, lt

  // Other names for the same wires on the sheet: Ain[31:0] = A_in; Bin[31:0] = B_in; Ein[31:0] = E_in;
  //   Min[31:0] = M_in; Win[31:0] = W_in
endmodule

module ALU_Input_Sel (
  input  [3:0] Opcode,
  output B_Sel
);

  wire and_1_out, comparator_1_gt, comparator_2_eq, comparator_2_gt, not_1_out, or_1_out;

  Comparator #(.width(4)) comparator_1 (.a(Opcode), .b(4'b0010), .gt(comparator_1_gt));  // open: eq, lt
  Comparator #(.width(4)) comparator_2 (
    .a(Opcode), .b(4'b0101), .gt(comparator_2_gt), .eq(comparator_2_eq));  // open: lt
  or or_1 (or_1_out, comparator_2_eq, comparator_2_gt);
  not not_1 (not_1_out, or_1_out);
  and and_1 (and_1_out, comparator_1_gt, not_1_out);
  Multiplexer #(.enable("false")) multiplexer_1 (.in0(1'b0), .in1(1'b1), .out(B_Sel), .sel(and_1_out));
endmodule

module BEQ_SW (
  input  [3:0] OP_INPUT,
  output OUTPUT
);

  wire comparator_1_eq, comparator_2_eq;

  Comparator #(.width(4)) comparator_1 (.a(OP_INPUT), .b(4'b0100), .eq(comparator_1_eq));  // open: gt, lt
  Comparator #(.width(4)) comparator_2 (.a(OP_INPUT), .b(4'b0101), .eq(comparator_2_eq));  // open: gt, lt
  or or_1 (OUTPUT, comparator_1_eq, comparator_2_eq);

  // Notes on the sheet:
  //   SW
  //   BEQ
endmodule

module Control_SIG (
  input  [3:0] Opcode,
  output WrEn,
  output JALR,
  output BEQ,
  output SW,
  output LW,
  output [1:0] FUNC,
  output NAND,
  output OFF,
  output HALT
);

  ROM #(.addrWidth(4), .dataWidth(10)) rom_1 (
    .addr(Opcode), .data({HALT, OFF, NAND, FUNC, LW, SW, BEQ, JALR, WrEn}));  // open: sel

  // Notes on the sheet:
  //   contents of rom_1 (hex, n*v repeats v):
  //   1 a1 101 111 108 44 3 200
endmodule

module LW_STALL (
  input  LW_EX,
  input  [3:0] LW_DEST,
  input  [3:0] A_REG,
  input  [3:0] B_REG,
  input  [3:0] ID_OP,
  input  sw_ID,
  output stall,
  output NOOP
);

  wire and_1_out, and_2_out, and_3_out, comparator_1_eq, comparator_2_eq, comparator_3_eq, multiplexer_1_out,
       not_1_out, or_1_out;

  Comparator #(.width(4)) comparator_1 (.a(A_REG), .b(LW_DEST), .eq(comparator_1_eq));  // open: gt, lt
  Comparator #(.width(4)) comparator_2 (.a(B_REG), .b(LW_DEST), .eq(comparator_2_eq));  // open: gt, lt
  or or_1 (or_1_out, comparator_1_eq, comparator_2_eq);
  Comparator #(.width(4)) comparator_3 (.a(LW_DEST), .b(4'b0000), .eq(comparator_3_eq));  // open: gt, lt
  and and_1 (and_1_out, LW_EX, or_1_out);
  and and_2 (and_2_out, comparator_2_eq, LW_EX);
  and and_3 (and_3_out, LW_EX, comparator_3_eq);
  not not_1 (not_1_out, and_3_out);
  Multiplexer #(.enable("false")) multiplexer_1 (
    .in0(and_1_out), .in1(and_2_out), .out(multiplexer_1_out), .sel(sw_ID));
  and and_4 (NOOP, not_1_out, multiplexer_1_out);

  assign stall = NOOP;
endmodule
